# Fritzing sketch ble_pointer (saved by Fritzing 0.9.6b)
breadboards: 1

parts:
  Mod1 = Raspberry Pi Pico W
  Part1 = InvenSense MPU6050
  S1 = Momentary Switch [package=ksa_sealed_tac_switch]
  S2 = Momentary Switch [package=ksa_sealed_tac_switch]

nets:
  N1: Mod1.pin_3, Mod1.pin_8, Mod1.pin_13, Mod1.pin_18, Mod1.pin_23, Mod1.pin_28, Mod1.pin_33, Mod1.pin_38, Part1.GND, S1.1, S1.2, S2.1, S2.2
  N2: Mod1.pin_6, Part1.SDA
  N3: Mod1.pin_7, Part1.SCL
  N4: Mod1.pin_20, S1.3, S1.4
  N5: Mod1.pin_21, S2.3, S2.4
  N6: Mod1.pin_36, Part1.VCC

custom parts:
  Raspberry Pi Pico W: Raspberry Pi Pico W. Based around the RP2040 microcontroller the Pico W is a low cost microcontroller device bringing Raspberry Pi quality, cost, and easy of use to the microcontroller space. The areas marked KEEPOUT in pcb silkscreen should not have traces running through them to avoid shorts on a soldered in module!
