# Fritzing sketch wiz850io (saved by Fritzing 0.9.3b)
breadboards: 1

parts:
  WIZ820io1 = WIZ820io [part_number=WIZ820io]
  Mod1 = Raspberry Pi Pico

nets:
  GND: WIZ820io1.GND, WIZ820io1.VIN, Mod1.pin_3, Mod1.pin_8, Mod1.pin_13, Mod1.pin_18, Mod1.pin_23, Mod1.pin_28, Mod1.pin_33, Mod1.pin_36, Mod1.pin_38, Mod1.pin_42
  N1: WIZ820io1.MOSI, Mod1.pin_5
  N2: WIZ820io1.SCLK, Mod1.pin_4
  N3: WIZ820io1.nSS, WIZ820io1.nINT, Mod1.pin_7
  N4: WIZ820io1.MISO, WIZ820io1.nRESET, Mod1.pin_6, Mod1.pin_9

custom parts:
  Raspberry Pi Pico: Raspberry Pi Pico. Based around the RP2040 microcontroller the Pico is a low cost microcontroller device bringing Raspberry Pi quality, cost, and easy of use to the microcontroller space. Jan 2021, Split part in to two versions: tht (this one) and SMD. This one will drill holes for a .1 in header in pcb to allow plugging in the module as well as providing pads to solder the module to the top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
