# Fritzing sketch pi-and-pico-uart-and-dht-sensor (saved by Fritzing 0.9.4)
breadboards: 1

parts:
  Mod1 = Raspberry Pi Picoboard
  RHT1 = Humidity and Temperature Sensor RHT03
  R1 = Resistor [tolerance=±5% resistance=10k package="2512 [SMD]"]
  Mod2 = Raspberry Pi 4B

nets:
  GND: Mod1.GND, RHT1.GND_2, Mod2.GND
  3V3: Mod1.3V3, RHT1.Vcc, R1.Pin_0
  N1: Mod1.GP15, RHT1.Data-signal, R1.Pin_1
  N2: Mod1.GP1, Mod2.GPIO14
  N3: Mod1.GP0, Mod2.GPIO15

custom parts:
  Raspberry Pi Picoboard: The Raspberry Pi Picoboard. Based around the Raspberry Pi Pico 2040 micro-controller the Picoboard is a low cost micro-controller device bringin the Raspberry Pi quality, cost, and easy of use to the micro-controller space.
