# Fritzing sketch 24lc32_i2c (saved by Fritzing 0.9.6b)
breadboards: 1

parts:
  Adafruit_24LC32_I2C_EEPROM1 = Adafruit 24LC32 I2C EEPROM Breakout - 32Kbit / 4 KB - Stemma QT [part_number=#5146]
  Pico/Pico2_Mod_1 = Raspberry Pi Pico or Pico 2

nets:
  VCC: Adafruit_24LC32_I2C_EEPROM1.VCC, Adafruit_24LC32_I2C_EEPROM1.3.3V, Pico/Pico2_Mod_1.pin_36
  N1: Adafruit_24LC32_I2C_EEPROM1.GND, Pico/Pico2_Mod_1.pin_3, Pico/Pico2_Mod_1.pin_8, Pico/Pico2_Mod_1.pin_13, Pico/Pico2_Mod_1.pin_18, Pico/Pico2_Mod_1.pin_23, Pico/Pico2_Mod_1.pin_28, Pico/Pico2_Mod_1.pin_33, Pico/Pico2_Mod_1.pin_38
  N2: Adafruit_24LC32_I2C_EEPROM1.SCL, Pico/Pico2_Mod_1.pin_7
  N3: Adafruit_24LC32_I2C_EEPROM1.SDA, Adafruit_24LC32_I2C_EEPROM1.WP, Pico/Pico2_Mod_1.pin_6

custom parts:
  Adafruit 24LC32 I2C EEPROM Breakout - 32Kbit / 4 KB - Stemma QT: If you want to store calibration values, MAC addresses, non-secure access tokens, or other unique identifiers, EEPROM storage is a great option. EEPROM is long lasting, and doesn't need to be written in pages - a single byte can be written at once (unlike with flash memory!) EEPROM storage persists even when the power goes out, and can be over-written literally one million times. Some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
  Raspberry Pi Pico or Pico 2: Raspberry Pi Pico and Pico 2. Based around the RP2040 and RP2350 microcontrollers respectively, Picos are low cost microcontroller device bringing Raspberry Pi quality, cost, and easy of use to the microcontroller space. Jan 2021, Split part in to two versions: tht (this one) and SMD. This one will drill holes for a .1 in header in pcb to allow plugging in the module as well as providing pads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
