# Fritzing sketch ina228_i2c (saved by Fritzing 0.9.6b)
breadboards: 1

parts:
  R1 = Resistor [tolerance=±5% power=0.25 resistance=330 package=THT]
  LED1 = LED - 5mm [color="Red (633nm)" current=30mA package="5 mm [THT]"]
  Adafruit_INA228_I2C_Power_Monitor1 = Adafruit INA228 I2C Power Monitor [part_number=#5832]
  Pico/Pico2_Mod_1 = Raspberry Pi Pico or Pico 2

nets:
  N1: R1.Pin_0, Adafruit_INA228_I2C_Power_Monitor1.VBUS, Pico/Pico2_Mod_1.pin_4
  N2: R1.Pin_1, LED1.anode
  N3: LED1.cathode, Adafruit_INA228_I2C_Power_Monitor1.VIN+
  N4: Adafruit_INA228_I2C_Power_Monitor1.VCC, Pico/Pico2_Mod_1.pin_36
  N5: Adafruit_INA228_I2C_Power_Monitor1.GND, Adafruit_INA228_I2C_Power_Monitor1.VIN-, Pico/Pico2_Mod_1.pin_3, Pico/Pico2_Mod_1.pin_8, Pico/Pico2_Mod_1.pin_13, Pico/Pico2_Mod_1.pin_18, Pico/Pico2_Mod_1.pin_23, Pico/Pico2_Mod_1.pin_28, Pico/Pico2_Mod_1.pin_33, Pico/Pico2_Mod_1.pin_38
  N6: Adafruit_INA228_I2C_Power_Monitor1.SCL, Pico/Pico2_Mod_1.pin_7
  N7: Adafruit_INA228_I2C_Power_Monitor1.SDA, Pico/Pico2_Mod_1.pin_6

custom parts:
  Adafruit INA228 I2C Power Monitor: The INA228 is an amazing power monitoring chip, with best-of-everything support: up to 85VDC common-mode, high or low side measurements, 20-bit (!) ADC for precision measurements from milliamp to Amp, and I2C interface for easy configuration of alerts, oversampling, gain adjustments and more! This breakout board may well be the last current sensing solution you every need to buy. Not only can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
  Raspberry Pi Pico or Pico 2: Raspberry Pi Pico and Pico 2. Based around the RP2040 and RP2350 microcontrollers respectively, Picos are low cost microcontroller device bringing Raspberry Pi quality, cost, and easy of use to the microcontroller space. Jan 2021, Split part in to two versions: tht (this one) and SMD. This one will drill holes for a .1 in header in pcb to allow plugging in the module as well as providing pads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
