# Fritzing sketch ina260_i2c (saved by Fritzing 1.0.5)
breadboards: 1

parts:
  Pico_H1 = Raspberry Pi Pico H
  Part1 = INA 260
  Pico_H2 = Raspberry Pi Pico H

nets:
  N1: Pico_H1.VSYS, Part1.VCC, Part1.IN+
  GND: Pico_H1.GND, Part1.GND, Pico_H2.GND
  N2: Pico_H1.GP5, Part1.SCL
  N3: Pico_H1.GP4, Part1.SDA
  N4: Part1.IN-, Pico_H2.VSYS

notes:
  High side power measurement using ina260
  powered by analyser
  device under test
  analyser device
  powered by usb

custom parts:
  Raspberry Pi Pico H: Raspberry Pi Pico H. Based around the RP2040 microcontroller the Pico H is a low cost microcontroller device bringing Raspberry Pi quality, cost, and easy of use to the microcontroller space.
  INA 260: Rev. B, add copy
