# Fritzing sketch lcd_1602_i2c (saved by Fritzing 0.9.3b)
breadboards: 1

parts:
  Mod1 = Raspberry Pi Picoboard
  Part1 = LCD1602-I2C

nets:
  GND: Mod1.GND, Part1.GND
  3V3: Mod1.3V3, Part1.VCC
  N1: Mod1.GP5, Part1.SCL
  N2: Mod1.GP4, Part1.SDA

custom parts:
  Raspberry Pi Picoboard: The Raspberry Pi Picoboard. Based around the Raspberry Pi Pico 2040 micro-controller the Picoboard is a low cost micro-controller device bringin the Raspberry Pi quality, cost, and easy of use to the micro-controller space.
  LCD1602-I2C: A standard character display, usually with 2x16 characters. Comes in many colors with LCM1602 IIC attached.
