# Fritzing sketch mpl3115a2_i2c (saved by Fritzing 0.9.3b)
breadboards: 1

parts:
  Mod1 = Raspberry Pi Pico
  Part1 = MPL3115A2 I2C Barometric Pressure, Altitude, Temperature Sensor

nets:
  N1: Mod1.pin_3, Mod1.pin_8, Mod1.pin_13, Mod1.pin_18, Mod1.pin_23, Mod1.pin_28, Mod1.pin_33, Mod1.pin_38, Part1.GND
  N2: Mod1.pin_6, Part1.SDA
  N3: Mod1.pin_7, Part1.SCL
  N4: Mod1.pin_21, Part1.INT1
  N5: Mod1.pin_22, Part1.INT2
  N6: Mod1.pin_36, Part1.VIN

custom parts:
  Raspberry Pi Pico: Raspberry Pi Pico. Based around the RP2040 microcontroller the Pico is a low cost microcontroller device bringing Raspberry Pi quality, cost, and easy of use to the microcontroller space. Jan 2021, Split part in to two versions: tht (this one) and SMD. This one will drill holes for a .1 in header in pcb to allow plugging in the module as well as providing pads to solder the module to the top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
  MPL3115A2 I2C Barometric Pressure, Altitude, Temperature Sensor: This pressure sensor from Freescale is a great low-cost sensing solution for precision measurement of barometric pressure and altitude. The MPL3115A2 has a typical 1.5 Pascal resolution, which can resolve altitude at 0.3 meters (compare to the BMP180 which can do 0.17m). It has some upsides compared to the BMP180, such as interrupt outputs for ultra-low power usage, and its also a heck of a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
