# Fritzing sketch mpu6050_i2c (saved by Fritzing 0.9.3b)
breadboards: 1

parts:
  Mod1 = Raspberry Pi Picoboard
  GY1 = MPU-6050 Board GY-521 [form="♀ (female)" package=THT]

nets:
  N1: Mod1.GND, GY1.pin2
  N2: Mod1.3V3, GY1.pin1
  N3: Mod1.GP5, GY1.pin3
  N4: Mod1.GP4, GY1.pin4

custom parts:
  Raspberry Pi Picoboard: The Raspberry Pi Picoboard. Based around the Raspberry Pi Pico 2040 micro-controller the Picoboard is a low cost micro-controller device bringin the Raspberry Pi quality, cost, and easy of use to the micro-controller space.
  MPU-6050 Board GY-521: Acelerometro y Giroscopio MPU-6050 Board GY-521
