# Fritzing sketch ssd1306_i2c (saved by Fritzing 0.9.3b)
breadboards: 1

parts:
  Mod1 = Raspberry Pi Picoboard
  OLED1 = OLED 128x64 I2C Monochrome Display

nets:
  GND: Mod1.GND, OLED1.GND
  3V3: Mod1.3V3, OLED1.VDD
  N1: Mod1.GP13, OLED1.SCK
  N2: Mod1.GP12, OLED1.SDA

custom parts:
  Raspberry Pi Picoboard: The Raspberry Pi Picoboard. Based around the Raspberry Pi Pico 2040 micro-controller the Picoboard is a low cost micro-controller device bringin the Raspberry Pi quality, cost, and easy of use to the micro-controller space.
