# Fritzing sketch 7_segment_wiring (saved by Fritzing 0.9.6b)
breadboards: 1

parts:
  Mod1 = Raspberry Pi Pico  # not connected
  Q1 = NPN-Transistor [package="TO92 [THT]"]
  R1 = Resistor [tolerance=±5% power=0.25 resistance=180 package=THT]
  Q2 = NPN-Transistor [package="TO92 [THT]"]
  LED1 = 7-SEGMENT-4DIGIT-YOUNGSUN [package=7-segment-4digit-youngsun-longpads]
  Q3 = NPN-Transistor [package="TO92 [THT]"]
  Q4 = NPN-Transistor [package="TO92 [THT]"]
  Q5 = NPN-Transistor [package="TO92 [THT]"]
  Q6 = NPN-Transistor [package="TO92 [THT]"]
  Q7 = NPN-Transistor [package="TO92 [THT]"]
  Q8 = NPN-Transistor [package="TO92 [THT]"]
  R2 = Resistor [tolerance=±5% power=0.25 resistance=180 package=THT]
  R3 = Resistor [tolerance=±5% power=0.25 resistance=180 package=THT]
  R4 = Resistor [tolerance=±5% power=0.25 resistance=180 package=THT]
  R5 = Resistor [tolerance=±5% power=0.25 resistance=180 package=THT]
  R6 = Resistor [tolerance=±5% power=0.25 resistance=180 package=THT]
  R7 = Resistor [tolerance=±5% power=0.25 resistance=180 package=THT]
  R8 = Resistor [tolerance=±5% power=0.25 resistance=180 package=THT]
  Q9 = NPN-Transistor [package="TO92 [THT]"]
  R9 = Resistor [tolerance=±5% power=0.25 resistance=220 package=THT]
  Q10 = PNP-Transistor [package="SOT-23 [SMD]"]
  Q11 = NPN-Transistor [package="TO92 [THT]"]
  R10 = Resistor [tolerance=±5% power=0.25 resistance=220 package=THT]
  Q12 = PNP-Transistor [package="SOT-23 [SMD]"]
  Q13 = PNP-Transistor [package="SOT-23 [SMD]"]
  Q14 = PNP-Transistor [package="SOT-23 [SMD]"]
  Q15 = NPN-Transistor [package="TO92 [THT]"]
  Q16 = NPN-Transistor [package="TO92 [THT]"]
  R11 = Resistor [tolerance=±5% power=0.25 resistance=220 package=THT]
  R12 = Resistor [tolerance=±5% power=0.25 resistance=220 package=THT]
  Q17 = NPN-Transistor [package="TO92 [THT]"]  # not connected
  Q18 = PNP-Transistor [package="SOT-23 [SMD]"]  # not connected

nets:
  N1: Q1.E, R1.Pin_1
  N2: Q1.C, LED1.E
  N3: R1.Pin_0, R2.Pin_0, R3.Pin_0, R4.Pin_0, R5.Pin_0, R6.Pin_0, R7.Pin_0, R8.Pin_0, R9.Pin_0, R10.Pin_0, R11.Pin_0
  N4: Q2.E, R8.Pin_1
  N5: Q2.C, LED1.D
  N6: LED1.DIG1, Q14.1
  N7: LED1.DIG2, Q13.1
  N8: LED1.DIG3, Q12.1
  N9: LED1.DP, Q8.C
  N10: LED1.DIG4, Q10.1
  N11: LED1.F, Q3.C
  N12: LED1.COL-C, LED1.C, Q5.C
  N13: LED1.A, Q4.C
  N14: LED1.G, Q6.C
  N15: LED1.B, Q7.C
  N16: Q3.E, R3.Pin_1
  N17: Q4.E, R5.Pin_1
  N18: Q5.E, R4.Pin_1
  N19: Q6.E, R6.Pin_1
  N20: Q7.E, R7.Pin_1
  N21: Q8.E, R2.Pin_1
  N22: Q9.E, R9.Pin_1
  N23: Q9.C, Q10.0
  N24: Q10.2, Q12.2, Q13.2, Q14.2
  N25: Q11.E, R10.Pin_1
  N26: Q11.C, Q12.0
  N27: Q13.0, Q15.C
  N28: Q14.0, Q16.C
  N29: Q15.E, R12.Pin_1
  N30: Q16.E, R11.Pin_1

notes:
  E
  D
  B
  G
  A
  C
  F
  dp
  4
  3
  2
  1
  EBC
  +5V
  0V
  NPN Transistors
  PNP Transistors

custom parts:
  Raspberry Pi Pico: Raspberry Pi Pico. Based around the RP2040 microcontroller the Pico is a low cost microcontroller device bringing Raspberry Pi quality, cost, and easy of use to the microcontroller space. Jan 2021, Split part in to two versions: tht (this one) and SMD. This one will drill holes for a .1 in header in pcb to allow plugging in the module as well as providing pads to solder the module to the top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
  7-SEGMENT-4DIGIT-YOUNGSUN: This is a part for the 4-Digit 7-segment LEDs from Young Sun. Different from the Digikey LEDs, all 16 pins are used. The LONGPADS Variant is used for a test jig, but you may like it because there is more pad to solder to. If you are concerned about routing space, the standard works just fine though.
