# Fritzing sketch eink_mono_spi (saved by Fritzing 0.9.3b)
breadboards: 1

parts:
  Mod1 = Raspberry Pi Pico
  Part1 = Adafruit 1.54" Tri-Color eInk / ePaper Display with SRAM [part_number=3625]

nets:
  N1: Mod1.pin_3, Mod1.pin_8, Mod1.pin_13, Mod1.pin_18, Mod1.pin_23, Mod1.pin_28, Mod1.pin_33, Mod1.pin_38, Mod1.pin_42, Part1.GND
  N2: Mod1.pin_15, Part1.RESET
  N3: Mod1.pin_16, Part1.BUSY
  N4: Mod1.pin_17, Part1.ENABLE
  N5: Mod1.pin_21, Part1.MISO
  N6: Mod1.pin_22, Part1.DISPCS
  N7: Mod1.pin_24, Part1.SCLK
  N8: Mod1.pin_25, Part1.MOSI
  N9: Mod1.pin_26, Part1.DC
  N10: Mod1.pin_27, Part1.SRAMCS
  N11: Mod1.pin_29, Part1.SDCS
  N12: Mod1.pin_36, Part1.VIN

custom parts:
  Raspberry Pi Pico: Raspberry Pi Pico. Based around the RP2040 microcontroller the Pico is a low cost microcontroller device bringing Raspberry Pi quality, cost, and easy of use to the microcontroller space. Jan 2021, Split part in to two versions: tht (this one) and SMD. This one will drill holes for a .1 in header in pcb to allow plugging in the module as well as providing pads to solder the module to the top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
  Adafruit 1.54" Tri-Color eInk / ePaper Display with SRAM: This small 1.54" tri-color display has 152x152 black and red ink pixels and a white-ish background. Using our Arduino library, you can create a 'frame buffer' with what pixels you want to have activated and then write that out to the display. We tossed a small SRAM chip on the back. This chip shares the SPI port the eInk display uses, so you only need one extra pin. And, no more frame-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
