# Fritzing sketch mpu9250_spi (saved by Fritzing 0.9.3b)
breadboards: 1

parts:
  Mod1 = Raspberry Pi Picoboard
  M1 = gy9250

nets:
  N1: Mod1.GND, M1.pin2
  N2: Mod1.3V3, M1.pin1
  N3: Mod1.GP7, M1.pin4
  N4: Mod1.GP6, M1.pin3
  N5: Mod1.GP5, M1.pin9
  N6: Mod1.GP4, M1.pin7

custom parts:
  Raspberry Pi Picoboard: The Raspberry Pi Picoboard. Based around the Raspberry Pi Pico 2040 micro-controller the Picoboard is a low cost micro-controller device bringin the Raspberry Pi quality, cost, and easy of use to the micro-controller space.
  gy9250: MPU-9250 module (three-axis gyroscope + three-axis acceleration + three-axis magnetic field). The generic model from ebay et. al. rather than the Sparkfun version.
