# Fritzing sketch lcd_uart (saved by Fritzing 0.9.3b)
breadboards: 1

parts:
  LCD1 = Adafruit Positive RGB 2x16 LCD  # not connected
  Part1 = Adafruit USB Serial Char LCD Backpack [part_number="Adafruit #784 and #782"]
  Mod1 = Raspberry Pi Pico

nets:
  N1: Part1.+3V3, Mod1.pin_36
  N2: Part1.GND, Mod1.pin_3, Mod1.pin_8, Mod1.pin_13, Mod1.pin_18, Mod1.pin_23, Mod1.pin_28, Mod1.pin_33, Mod1.pin_38
  N3: Part1.RX, Mod1.pin_11

custom parts:
  Adafruit Positive RGB 2x16 LCD: Adafruit Positive 2x16 LCD Display with RGB Backlight
  Adafruit USB Serial Char LCD Backpack: Adding a character display to your project or computer has never been easier with the new Adafruit USB or TTL serial backpack! This custom-designed PCB sits on the back of our 'standard' character LCD (16x2 or 20x4 sized) and does everything you could want: printing text, automatic scrolling, setting the backlight, adjusting contrast, making custom characters, turning on and off the cursor,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
  Raspberry Pi Pico: Raspberry Pi Pico. Based around the RP2040 microcontroller the Pico is a low cost microcontroller device bringing Raspberry Pi quality, cost, and easy of use to the microcontroller space. Jan 2021, Split part in to two versions: tht (this one) and SMD. This one will drill holes for a .1 in header in pcb to allow plugging in the module as well as providing pads to solder the module to the top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
